// Digital circuit ALU.dig as structural Verilog
module ALU (
  input  [7:0] Reg_A,
  input  [7:0] Reg_B,
  input  [2:0] Operation_Select,
  output Negative_Flag,
  output Zero_Flag,
  output Carry_Borrow_Flag,
  output [7:0] Result,
  output Overflow_Flag
);

  wire ADD_c_o, and_2_out, and_3_out, and_4_out, and_5_out, and_8_out, and_9_out, comparator_1_eq,
       comparator_2_eq, comparator_3_eq, comparator_4_eq, comparator_5_eq, comparator_6_eq, comparator_7_eq,
       comparator_8_eq, comparator_10_eq, comparator_11_eq, DEC_c_o, INC_c_o, or_2_out, or_3_out, SUB_c_o;
  wire [7:0] ADD_s, and_1_out, and_6_out, and_7_out, DEC_s, INC_s, not_1_out, not_2_out, not_3_out, or_1_out,
       Reg_A_7_out, Reg_B_7_out, Result_7_out, SUB_s, xnor_1_out, xor_1_out, xor_2_out;

  assign not_1_out = ~Reg_B;  // Not not_1, 8 bits wide
  Add #(.Bits(8)) ADD (.a(Reg_A), .b(Reg_B), .c_i(1'b0), .s(ADD_s), .c_o(ADD_c_o));
  Add #(.Bits(8)) SUB (.a(Reg_A), .b(not_1_out), .c_i(1'b1), .s(SUB_s), .c_o(SUB_c_o));
  Add #(.Bits(8)) INC (.a(Reg_A), .b(8'h1), .c_i(1'b0), .s(INC_s), .c_o(INC_c_o));
  Add #(.Bits(8)) DEC (.a(Reg_A), .b({8{1'b1}}), .c_i(1'b0), .s(DEC_s), .c_o(DEC_c_o));
  assign and_1_out = Reg_A & Reg_B;  // And and_1, 8 bits wide
  assign or_1_out = Reg_A | Reg_B;  // Or or_1, 8 bits wide
  assign xor_1_out = Reg_A ^ Reg_B;  // XOr xor_1, 8 bits wide
  assign not_2_out = ~Reg_A;  // Not not_2, 8 bits wide
  Multiplexer #(.Selector_Bits(3), .Bits(8)) multiplexer_1 (
    .sel(Operation_Select), .in_0(ADD_s), .in_1(SUB_s), .in_2(INC_s), .in_3(DEC_s), .in_4(and_1_out),
    .in_5(or_1_out), .in_6(xor_1_out), .in_7(not_2_out), .out(Result));
  Comparator #(.Bits(3)) comparator_1 (.a(Operation_Select), .b(3'b000), .eq(comparator_1_eq));  // open: gt, lt
  Comparator #(.Bits(3)) comparator_2 (.a(Operation_Select), .b(3'b001), .eq(comparator_2_eq));  // open: gt, lt
  Comparator #(.Bits(3)) comparator_3 (.a(Operation_Select), .b(3'b010), .eq(comparator_3_eq));  // open: gt, lt
  Comparator #(.Bits(3)) comparator_4 (.a(Operation_Select), .b(3'b011), .eq(comparator_4_eq));  // open: gt, lt
  Comparator #(.Bits(3)) comparator_5 (.a(Operation_Select), .b(3'b000), .eq(comparator_5_eq));  // open: gt, lt
  Comparator #(.Bits(3)) comparator_6 (.a(3'b010), .b(Operation_Select), .eq(comparator_6_eq));  // open: gt, lt
  Comparator #(.Bits(3)) comparator_7 (.a(Operation_Select), .b(3'b001), .eq(comparator_7_eq));  // open: gt, lt
  Comparator #(.Bits(3)) comparator_8 (.a(Operation_Select), .b(3'b011), .eq(comparator_8_eq));  // open: gt, lt
  and and_2 (and_2_out, ADD_c_o, comparator_1_eq);
  and and_3 (and_3_out, SUB_c_o, comparator_2_eq);
  and and_4 (and_4_out, INC_c_o, comparator_3_eq);
  and and_5 (and_5_out, comparator_4_eq, DEC_c_o);
  or or_2 (or_2_out, comparator_5_eq, comparator_6_eq);
  or or_3 (or_3_out, comparator_7_eq, comparator_8_eq);
  BarrelShifter #(.Bits(8), .direction("right")) Reg_A_7 (.in(Reg_A), .shift(4'b0111), .out(Reg_A_7_out));
  BarrelShifter #(.Bits(8), .direction("right")) Reg_B_7 (.in(Reg_B), .shift(4'b0111), .out(Reg_B_7_out));
  or or_4 (Carry_Borrow_Flag, and_2_out, and_3_out, and_4_out, and_5_out);
  assign xor_2_out = Result_7_out ^ Reg_A_7_out;  // XOr xor_2, 8 bits wide
  assign xnor_1_out = ~(Reg_A_7_out ^ Reg_B_7_out);  // XNOr xnor_1, 8 bits wide
  BarrelShifter #(.Bits(8), .direction("right")) Result_7 (.in(Result), .shift(4'b0111), .out(Result_7_out));
  Comparator #(.Bits(8)) comparator_9 (.a(Result), .b({8{1'b0}}), .eq(Zero_Flag));  // open: gt, lt
  assign not_3_out = ~xnor_1_out;  // Not not_3, 8 bits wide
  assign and_6_out = xor_2_out & xnor_1_out;  // And and_6, 8 bits wide
  assign and_7_out = xor_2_out & not_3_out;  // And and_7, 8 bits wide
  Comparator #(.Bits(8)) comparator_10 (.a(8'h1), .b(and_6_out), .eq(comparator_10_eq));  // open: gt, lt
  Comparator #(.Bits(8)) comparator_11 (.a(8'h1), .b(and_7_out), .eq(comparator_11_eq));  // open: gt, lt
  Comparator #(.Bits(8)) comparator_12 (.a(8'h1), .b(Result_7_out), .eq(Negative_Flag));  // open: gt, lt
  and and_8 (and_8_out, or_2_out, comparator_10_eq);
  and and_9 (and_9_out, comparator_11_eq, or_3_out);
  or or_5 (Overflow_Flag, and_8_out, and_9_out);
endmodule
